# Fritzing sketch dht_extension_v01 (saved by Fritzing 0.9.3b)
stripboards: 1

parts:
  S1 = Pushbutton [package=THT]
  R1 = Resistor [tolerance=±5% resistance=10k package="1206 [SMD]"]
  R2 = Resistor [tolerance=±5% resistance=10k package="1206 [SMD]"]
  RHT1 = Humidity and Temperature Sensor RHT03

nets:
  N1: S1.leg0, R2.Pin_1
  N2: S1.leg1, R2.Pin_0, RHT1.GND_2
  N3: R1.Pin_0, RHT1.Vcc
  N4: R1.Pin_1, RHT1.Data-signal
